# Fritzing sketch ardBeeQueenFritz (saved by Fritzing 0.9.2b)
breadboards: 1

parts:
  Part1 = Arduino Pro Mini v13
  Part2 = KY-019 5V Relay Module [package="Breakout board"]
  X1 = USB Connectors [package=usb-microb]
  Part3 = KY-019 5V Relay Module [package="Breakout board"]
  U1 = LCD-16X2 [package=lcd-16x2_noholes]
  DHT1 = DHT11 Humitidy and Temperature Sensor
  R2 = Trimmer Potentiometer [maximum_resistance=10kΩ package=THT]
  R3 = Resistor [tolerance=±5% resistance=220 package=THT]

nets:
  GND: Part1.GND, Part2.-, X1.GND, Part3.-, U1.VSS, U1.R_W, U1.K, DHT1.GND, R2.leg2
  N1: Part1.RAW, X1.VBUS
  VDD: Part1.VCC, Part2.+, Part3.+, U1.VDD, DHT1.VDD, R2.leg1, R3.Pin_1
  N2: Part1.D13/SCK, U1.RS
  N3: Part1.D12/MISO, U1.E
  N4: Part1.D11_PWM/MOSI, U1.DB4
  N5: Part1.D10_PWM/SS, U1.DB5
  N6: Part1.D9_PWM, U1.DB6
  N7: Part1.D8, U1.DB7
  N8: Part1.D4, Part3.S
  N9: Part1.D3_PWM, Part2.S
  N10: Part1.D2, DHT1.DATA
  N11: U1.VO, R2.wiper
  N12: U1.A, R3.Pin_0

custom parts:
  KY-019 5V Relay Module: KY-019 5V Relay module, used to control AC circuits.
  DHT11 Humitidy and Temperature Sensor: DHT11 Humidity and Temperature Sensor
